// Logisim project trab_arq.circ as structural Verilog: 1 circuit, main circuit main
module main (
  input  MSD,
  input  in_2,
  input  in_3,
  input  in_4,
  input  in_5,
  input  in_6,
  input  in_7,
  input  in_8,
  input  in_9,
  input  in_10,
  input  in_11,
  input  in_12,
  input  in_13,
  input  in_14,
  input  in_15,
  input  in_16,
  input  in_17,
  input  in_18,
  input  in_19,
  input  in_20,
  input  in_21,
  input  in_22,
  input  in_23,
  input  in_24,
  input  in_25,
  input  in_26,
  input  NEGATIVO,
  input  in_28,
  input  JNBJ,
  input  in_30,
  input  in_31,
  input  in_32,
  input  ZERO,
  input  in_34,
  input  JAMZ,
  input  LSD,
  output NEGATIVO_2,
  output ZERO_2,
  output out_39
);

  wire and_1_out, and_2_out, or_1_out;

  or or_1 (or_1_out, MSD, in_2, in_3, in_4, in_5, in_6, in_7, in_8, in_9, in_10, in_11, in_12, in_13, in_14, in_15, in_16, in_17, in_18, in_19, in_20, in_21, in_22, in_23, in_24, in_25, in_26, in_28, in_30, in_31, in_32, in_34, LSD);
  not not_1 (ZERO_2, or_1_out);
  and and_1 (and_1_out, NEGATIVO, JNBJ);
  and and_2 (and_2_out, ZERO, JAMZ);
  or or_2 (out_39, and_1_out, and_2_out);

  assign NEGATIVO_2 = MSD;

  // Notes on the sheet:
  //   CIRCUITO BIT ALTO
endmodule
